# Fritzing sketch SiloDemoCircuitDiagram (saved by Fritzing 0.9.3b)
breadboards: 1

parts:
  Part1 = Adafruit HUZZAH32 ESP32 Feather [part_number="Adafruit #3405"]
  Part2 = HX711 Weighing Sensor Module
  LED1 = RGB LED - (4 legs) [package="5 mm [THT]"]
  S1 = Round Pushbutton
  Load_Cell1 = Load Cell - Red/white/black/green

nets:
  N1: Part1.IO17, Part2.DO/RX
  N2: Part1.IO16, Part2.CK/TX
  GND: Part1.GND, Part2.GND, S1.leg0
  3.3V: Part1.3.3V, Part2.VCC, LED1.common_anode
  N3: Part1.IO13_A12, LED1.red_cathode
  N4: Part1.IO12_A11, LED1.green_cathode
  N5: Part1.IO27_A10, LED1.blue_cathode
  N6: Part1.IO15_A8, S1.leg1
  N7: Part2.E+, Load_Cell1.wire1
  N8: Part2.E-, Load_Cell1.wire3
  N9: Part2.A+, Load_Cell1.wire4
  N10: Part2.A-, Load_Cell1.wire2

notes:
  Check Letters A+ and A- switched on some boards

custom parts:
  Load Cell - Red/white/black/green: A rectangle load cell/weighting pressure Sensor with four wires - Red, white, black, green. Normally corresponding with E+, E-, A+, A- respectively.
